# Fritzing sketch AmmeterShield (saved by Fritzing 0.7.12b)
breadboards: 1

parts:
  D1 = Rectifier Diode [part_number=1N4148 package="300 mil [THT]"]
  D2 = Rectifier Diode [part_number=1N4148 package="300 mil [THT]"]
  J1 = screw terminal, 2 pins
  J2 = screw terminal, 2 pins
  D3 = Rectifier Diode [part_number=1N4148 package="300 mil [THT]"]
  D4 = Rectifier Diode [part_number=1N4148 package="300 mil [THT]"]
  D7 = Rectifier Diode [part_number=1N4148 package="300 mil [THT]"]
  D8 = Rectifier Diode [part_number=1N4148 package="300 mil [THT]"]
  C5 = Electrolytic Capacitor [capacitance=10µF package="100 mil [THT, electrolytic]"]
  C6 = Electrolytic Capacitor [capacitance=10µF package="100 mil [THT, electrolytic]"]
  Shield = Arduino
  J4 = screw terminal, 2 pins
  J3 = screw terminal, 2 pins
  IC1 = SOIC-14 [chip_label=LM324 package=SO]
  IC2 = SOIC-14 [chip_label=LM324 package=SO]
  IC3 = SO08 [chip_label=MAX1044 package=SO]
  R10 = Resistor [tolerance=±1% resistance=100k package="1206 [SMD]"]
  R1 = Resistor [tolerance=±1% resistance=10k package="1206 [SMD]"]
  R2 = Resistor [tolerance=±1% resistance=10k package="1206 [SMD]"]
  R3 = Resistor [tolerance=±1% resistance=10k package="1206 [SMD]"]
  R4 = Resistor [tolerance=±1% resistance=100k package="1206 [SMD]"]
  R6 = Resistor [tolerance=±1% resistance=10k package="1206 [SMD]"]
  R11 = Resistor [tolerance=±1% resistance=10k package="1206 [SMD]"]
  R15 = Resistor [tolerance=±1% resistance=100k package="1206 [SMD]"]
  C4 = Ceramic Capacitor [capacitance=10µF package="1206 [SMD, multilayer]"]
  C1 = Ceramic Capacitor [capacitance=10µF package="1206 [SMD, multilayer]"]
  R7 = Resistor [tolerance=±1% resistance=10k package="1206 [SMD]"]
  R5 = Resistor [tolerance=±1% resistance=100k package="1206 [SMD]"]
  R8 = Resistor [tolerance=±1% resistance=10k package="1206 [SMD]"]
  R12 = Resistor [tolerance=±1% resistance=10k package="1206 [SMD]"]
  R9 = Resistor [tolerance=±1% resistance=100k package="1206 [SMD]"]
  R14 = Resistor [tolerance=±1% resistance=100k package="1206 [SMD]"]
  R16 = Resistor [tolerance=±1% resistance=10k package="1206 [SMD]"]
  R13 = Resistor [tolerance=±1% resistance=10k package="1206 [SMD]"]
  R18 = Resistor [tolerance=±1% resistance=100k package="1206 [SMD]"]
  R19 = Resistor [tolerance=±1% resistance=100k package="1206 [SMD]"]
  R17 = Resistor [tolerance=±1% resistance=10k package="1206 [SMD]"]
  D5 = Rectifier Diode [part_number=1N4148 package="300 mil [THT]"]
  D6 = Rectifier Diode [part_number=1N4148 breakdown_voltage=3.6V package="300 mil [THT]"]
  C2 = Ceramic Capacitor [capacitance=10µF package="1206 [SMD, multilayer]"]
  C3 = Ceramic Capacitor [capacitance=10µF package="1206 [SMD, multilayer]"]
  C7 = Ceramic Capacitor [capacitance=100nF package="1206 [SMD, multilayer]"]
  R20 = Resistor [tolerance=±1% resistance=10k package="1206 [SMD]"]

nets:
  N1: D1.cathode, IC1.5, R2.Pin_1
  N2: D1.anode, IC1.1
  N3: D2.cathode, Shield.A0, R4.Pin_1, C1.1, R5.Pin_0
  N4: D2.anode, IC1.7
  N5: J1.pin1, R1.Pin_1
  GND: J1.pin2, J2.pin2, C6.+, Shield.GND, J4.pin2, J3.pin2, IC1.3, IC1.12, IC2.3, IC2.12, IC3.3, IC3.6, R10.Pin_1, R3.Pin_1, R15.Pin_1, C4.0, C1.0, R5.Pin_1, R8.Pin_0, R13.Pin_0, R19.Pin_1, R17.Pin_1, C2.0, C3.0, C7.0
  N6: J2.pin1, R6.Pin_0
  N7: D3.cathode, IC1.10, R7.Pin_0
  N8: D3.anode, IC1.14
  N9: D4.cathode, Shield.A1, R10.Pin_0, R9.Pin_1, C2.1
  N10: D4.anode, IC1.8
  N11: D7.cathode, IC2.5, R20.Pin_0
  N12: D7.anode, IC2.1
  N13: D8.cathode, Shield.A2, C4.1, R18.Pin_1, R19.Pin_0
  N14: D8.anode, IC2.7
  N15: C5.-, IC3.4
  N16: C5.+, IC3.2
  N17: C6.-, IC1.11, IC2.11, IC3.5
  N18: Shield.3V3, IC1.4, IC2.4, IC3.8, C7.1
  N19: Shield.A3, R15.Pin_0, R14.Pin_1, D6.cathode, C3.1
  N20: J4.pin1, R16.Pin_1
  N21: J3.pin1, R11.Pin_0
  N22: IC1.2, R1.Pin_0, R2.Pin_0
  N23: IC1.6, R3.Pin_0, R4.Pin_0
  N24: IC1.9, R8.Pin_1, R9.Pin_0
  N25: IC1.13, R6.Pin_1, R7.Pin_1
  N26: IC2.2, R16.Pin_0, R20.Pin_1
  N27: IC2.6, R18.Pin_0, R17.Pin_0
  N28: IC2.8, D6.anode
  N29: IC2.9, R14.Pin_0, R13.Pin_1
  N30: IC2.10, R12.Pin_0, D5.cathode
  N31: IC2.13, R11.Pin_1, R12.Pin_1
  N32: IC2.14, D5.anode

notes:
  Precision
  Ammeter
